# Fritzing sketch wiring_2560 (saved by Fritzing 0.9.3b)

parts:
  R1 = Resistor [tolerance=±5% resistance=330 package="2010 [SMD]"]
  LED2 = LED - 3mm [color="Red (633nm)" package="3 mm [THT]"]
  S3 = Momentary Switch [package=ksa_sealed_tac_switch]
  U1 = CC1101 [part_number=CC1101]
  Bauteil4 = ws2812b [package="smd 2812b"]
  Bauteil5 = ws2812b [package="smd 2812b"]
  Bauteil6 = Arduino Mega 2560 (Rev3)

nets:
  N1: R1.Pin_0, LED2.anode
  N2: R1.Pin_1, Bauteil6.D4_PWM
  VSS: LED2.cathode, S3.4, U1.2, Bauteil4.VSS, Bauteil5.VSS, Bauteil6.GND
  N3: S3.2, Bauteil6.D13_PWM
  N4: U1.1, Bauteil6.3V3
  N5: U1.3, Bauteil6.D51
  N6: U1.4, Bauteil6.D52
  N7: U1.5, Bauteil6.D50
  N8: U1.7, Bauteil6.D2_PWM
  N9: U1.8, Bauteil6.D53
  VDD: Bauteil4.VDD, Bauteil5.VDD, Bauteil6.5V
  N10: Bauteil4.DOUT, Bauteil5.DIN
  N11: Bauteil4.DIN, Bauteil6.D9_PWM
