# Fritzing sketch wiring_ProMini (saved by Fritzing 0.9.3b)

parts:
  Bauteil3 = Arduino Pro Mini (5V)
  R1 = Resistor [tolerance=±5% resistance=330 package="2010 [SMD]"]
  LED2 = LED - 3mm [color="Red (633nm)" package="3 mm [THT]"]
  S3 = Momentary Switch [package=ksa_sealed_tac_switch]
  U1 = CC1101 [part_number=CC1101]
  Bauteil4 = ws2812b [package="smd 2812b"]
  Bauteil5 = ws2812b [package="smd 2812b"]

nets:
  VDD: Bauteil3.RAW, Bauteil4.VDD, Bauteil5.VDD
  VSS: Bauteil3.GND, LED2.cathode, S3.3, U1.2, Bauteil4.VSS, Bauteil5.VSS
  N1: Bauteil3.VCC, U1.1
  N2: Bauteil3.SCK, U1.4
  N3: Bauteil3.MISO, U1.5
  N4: Bauteil3.MOSI, U1.3
  N5: Bauteil3.D10, U1.8
  N6: Bauteil3.D9, Bauteil4.DIN
  N7: Bauteil3.D8, S3.1
  N8: Bauteil3.D4, R1.Pin_1
  N9: Bauteil3.D2, U1.7
  N10: R1.Pin_0, LED2.anode
  N11: Bauteil4.DOUT, Bauteil5.DIN
